# Fritzing sketch circuitDiagram (saved by Fritzing 0.9.3b)
breadboards: 1

parts:
  J1 = STM32 Nucleo boards
  ShiftRegister2 = 74HC595 SMD [package="SO16 [SMD]"]
  MIDI = MIDI_CONN_FEMALE_SUPPORT [package=din_5_female_support]
  ShiftRegister1 = 74HC595 SMD [package="SO16 [SMD]"]
  Sustain_Pedal = 3.5mm Audio Jack [package=audio-jack-3.5mm-smd]  # not connected
  PitchBend = Rotary Potentiometer (Small) [package=THT]  # not connected
  ModWheel = Rotary Potentiometer (Small) [maximum_resistance=100kΩ package=THT]  # not connected

nets:
  5V: J1.SWDIO, ShiftRegister2.MR, ShiftRegister2.VCC, ShiftRegister1.MR, ShiftRegister1.VCC
  GND: J1.GND, ShiftRegister2.GND, ShiftRegister2.OE, ShiftRegister1.GND, ShiftRegister1.OE
  N1: J1.PB6, MIDI.MIDI_IN
  N2: J1.PA9, ShiftRegister2.SH_CP, ShiftRegister1.SH_CP
  N3: J1.PA8, ShiftRegister2.ST_CP, ShiftRegister1.ST_CP
  N4: J1.PB10, ShiftRegister1.DS
  N5: J1.PA10, MIDI.MIDI_OUT
  T0 R: J1.PC10
  T1 R: J1.PC12
  T2 R: J1.PA13
  T3 R: J1.PA14
  T4 R: J1.PA15
  T5 R: J1.PB7
  T6 R: J1.PC2
  T7 R: J1.PC3
  BR4/BR9: ShiftRegister2.Q1
  MK10: ShiftRegister2.Q2
  BR10: ShiftRegister2.Q3
  N6: ShiftRegister2.DS, ShiftRegister1.Q7'
  MK4/MK9: ShiftRegister2.Q0
  BR0/BR5: ShiftRegister1.Q1
  MK1/MK6: ShiftRegister1.Q2
  BR1/BR6: ShiftRegister1.Q3
  MK2/MK7: ShiftRegister1.Q4
  BR2/BR7: ShiftRegister1.Q5
  MK3/MK8: ShiftRegister1.Q6
  BR3/BR8: ShiftRegister1.Q7
  MK0/MK5: ShiftRegister1.Q0

notes:
  grnd & pwr
