# Fritzing sketch veroboardDesign (saved by Fritzing 0.9.3b)
circuit board: 8.46667cm x 5.64444cm
breadboards: 1
perfboards: 2

parts:
  U1 = 74HC595 [package="DIP16 [THT]"]
  U2 = 74HC595 [package="DIP16 [THT]"]
  J1 = STM32 Nucleo boards
  JP2 = Header 1 [package=1x01_offset]  # not connected
  JP12 = Header 8 [package=1x08_smd]
  JP13 = Header 1 [package=1x01_offset]  # not connected
  JP14 = Header 1 [package=1x01_offset]  # not connected
  JP15 = Header 8 [package=1x08_smd]  # not connected
  JP16 = Header 1 [package=1x01_offset]  # not connected
  JP17 = Header 8 [package=1x08_smd]
  JP18 = Header 1 [package=1x01_offset]  # not connected
  JP19 = Header 1 [package=1x01_offset]  # not connected
  JP20 = Header 8 [package=1x08_smd]  # not connected
  JP21 = Header 1 [package=1x01_offset]  # not connected
  JP22 = Header 1 [package=1x01_offset]  # not connected
  JP23 = Header 8 [package=1x08_smd]  # not connected
  JP24 = Header 8 [package=1x08_smd]  # not connected
  JP25 = Header 1 [package=1x01_offset]  # not connected
  JP26 = Header 1 [package=1x01_offset]  # not connected
  JP27 = Header 1 [package=1x01_offset]  # not connected
  JP28 = Header 1 [package=1x01_offset]  # not connected
  JP29 = Header 8 [package=1x08_smd]  # not connected
  JP30 = Header 8 [package=1x08_smd]  # not connected
  JP31 = Header 1 [package=1x01_offset]  # not connected
  U3 = 74HC595 SMD [package="SO16 [SMD]"]
  U4 = 74HC595 SMD [package="SO16 [SMD]"]
  DIN1 = DIN-5 jack (MIDI) [package=THT]
  R1 = Resistor [tolerance=±5% resistance=2.2k package="2010 [SMD]"]
  J2 = female pin header, 19 pins [form="♀ (female)"]  # not connected
  J3 = female pin header, 19 pins [form="♀ (female)"]  # not connected
  J4 = female pin header, 19 pins [form="♀ (female)"]  # not connected
  J5 = female pin header, 19 pins [form="♀ (female)"]  # not connected
  U5 = 74HC595 [package="DIP16 [THT]"]  # not connected

nets:
  N1: U1.Q7', U2.DS
  VCC: U1.MR, U1.VCC, U2.MR, U2.VCC, J1.5V
  N2: U1.SH_CP, U2.SH_CP, J1.PB10
  N3: U1.ST_CP, U2.ST_CP, J1.PA8
  N4: U1.OE, U2.OE, J1.GND
  N5: U1.DS, J1.PA9
  N6: JP12.1, U3.ST_CP, U4.ST_CP
  N7: JP12.2, U3.SH_CP, U4.SH_CP
  N8: JP17.2, DIN1.2
  N9: JP17.6, DIN1.5
  N10: JP17.8, U3.DS
  GND: U3.GND, U3.OE, U4.GND, U4.OE
  N11: U3.Q7', U4.DS
  VCC_2: U3.VCC, U4.MR, U4.VCC, R1.Pin_0
  N12: DIN1.4, R1.Pin_1
