# Fritzing sketch veroboardDesign2 (saved by Fritzing 0.9.3b)
circuit board: 8.46667cm x 5.64444cm
breadboards: 1
perfboards: 1

parts:
  U1 = 74HC595 [package="DIP16 [THT]"]
  U2 = 74HC595 [package="DIP16 [THT]"]
  J1 = STM32 Nucleo boards
  JP2 = Header 1 [package=1x01_offset]  # not connected
  JP12 = Header 8 [package=1x08_smd]  # not connected
  JP13 = Header 1 [package=1x01_offset]  # not connected
  JP14 = Header 1 [package=1x01_offset]  # not connected
  JP15 = Header 8 [package=1x08_smd]  # not connected
  JP16 = Header 1 [package=1x01_offset]  # not connected
  JP17 = Header 8 [package=1x08_smd]  # not connected
  JP18 = Header 1 [package=1x01_offset]  # not connected
  JP19 = Header 1 [package=1x01_offset]  # not connected
  JP20 = Header 8 [package=1x08_smd]  # not connected
  JP21 = Header 1 [package=1x01_offset]  # not connected
  JP22 = Header 1 [package=1x01_offset]  # not connected
  JP23 = Header 8 [package=1x08_smd]
  JP24 = Header 8 [package=1x08_smd]  # not connected
  JP25 = Header 1 [package=1x01_offset]  # not connected
  JP26 = Header 1 [package=1x01_offset]  # not connected
  JP27 = Header 1 [package=1x01_offset]  # not connected
  JP28 = Header 1 [package=1x01_offset]  # not connected
  JP29 = Header 8 [package=1x08_smd]  # not connected
  JP30 = Header 8 [package=1x08_smd]
  JP31 = Header 1 [package=1x01_offset]  # not connected
  U3 = 74HC595 SMD [package="SO16 [SMD]"]
  U4 = 74HC595 SMD [package="SO16 [SMD]"]
  DIN1 = DIN-5 jack (MIDI) [package=THT]
  R1 = Resistor [tolerance=±5% resistance=2.2k package="2010 [SMD]"]
  J2 = longpad pin header, 4 pins [form="long pad"]
  J3 = shrouded pin header, 20 pins [form="♂ (shrouded male)"]  # not connected

nets:
  N1: U1.Q7', U2.DS
  VCC: U1.MR, U1.VCC, U2.MR, U2.VCC, J1.5V
  N2: U1.SH_CP, U2.SH_CP, J1.PB10
  N3: U1.ST_CP, U2.ST_CP, J1.PA8
  N4: U1.OE, U2.OE, J1.GND
  N5: U1.DS, J1.PA9
  N6: JP23.7, J2.pin3
  N7: JP23.8, J2.pin4
  N8: JP30.8, J2.pin2
  GND: U3.GND, U3.OE, U4.GND, U4.OE
  N9: U3.Q7', U4.DS
  N10: U3.SH_CP, U4.SH_CP
  N11: U3.ST_CP, U4.ST_CP
  VCC_2: U3.VCC, U4.MR, U4.VCC, R1.Pin_0
  N12: DIN1.4, R1.Pin_1

notes:
  mod & pitch
